# Fritzing sketch sketch (saved by Fritzing 0.9.3b)
breadboards: 1

parts:
  LED_2 = LED - 5mm [color="White (8000K)" package="5 mm [THT]"]
  Raspberry_Pi_1 = Raspberry Pi 3 [part_number=RPI-3-V1.2]
  R3 = Resistor [tolerance=±5% resistance=100 package=THT]
  R2 = Resistor [tolerance=±5% resistance=100 package=THT]
  LED_3 = LED - 5mm [color="Green (570nm)" package="5 mm [THT]"]
  R4 = Resistor [tolerance=±5% resistance=100 package=THT]
  LED_4 = LED - 5mm [color="Yellow (595nm)" package="5 mm [THT]"]

nets:
  N1: LED_2.cathode, R2.Pin_1
  N2: LED_2.anode, Raspberry_Pi_1.GPIO13
  N3: Raspberry_Pi_1.GPIO5, LED_4.anode
  N4: Raspberry_Pi_1.GPIO6, LED_3.anode
  N5: Raspberry_Pi_1.GND, R3.Pin_0, R2.Pin_0, R4.Pin_0
  N6: R3.Pin_1, LED_4.cathode
  N7: LED_3.cathode, R4.Pin_1

notes:
  LED 3 (flash_led_pin)
  LED 1 (startup_led_pin)
  LED 2 (preview_led_pin)
