# Fritzing sketch sketch (saved by Fritzing 0.9.3b)
breadboards: 1

parts:
  LED_2 = LED - 5mm [color="Red (633nm)" package="5 mm [THT]"]
  Raspberry_Pi_1 = Raspberry Pi 3 [part_number=RPI-3-V1.2]
  LED_1 = LED - 5mm [color="Blue (470nm)" package="5 mm [THT]"]
  R3 = Resistor [tolerance=±5% resistance=100 package=THT]
  R2 = Resistor [tolerance=±5% resistance=100 package=THT]
  R4 = Resistor [tolerance=±5% resistance=100 package=THT]
  LED_3 = LED - 5mm [color="Blue (470nm)" package="5 mm [THT]"]

nets:
  N1: LED_2.cathode, R2.Pin_1
  N2: LED_2.anode, Raspberry_Pi_1.GPIO22
  N3: Raspberry_Pi_1.GPIO4, LED_1.anode
  N4: Raspberry_Pi_1.GND, R3.Pin_0, R2.Pin_0, R4.Pin_0
  N5: LED_1.cathode, R3.Pin_1
  N6: R4.Pin_1, LED_3.cathode

notes:
  LED 2 (print_led_pin)
  LED 1 (picture_led_pin)
